// Digital circuit cpu.dig as structural Verilog
module cpu (
  input  clk,
  output [31:0] ReadData1,
  output [31:0] ReadData2
);

  wire [31:0] add_1_s, PC_q;

  Register #(.Bits(32), .isProgramCounter("true")) PC (.D(add_1_s), .C(clk), .en(1'b1), .Q(PC_q));
  Add #(.Bits(32)) add_1 (.a(32'h4), .b(PC_q), .c_i(1'b0), .s(add_1_s));  // open: c_o
  ROM #(.AddrBits(10), .isProgramMemory("true"), .Bits(32)) Instruction_Memory (.A(PC_q[11:2]), .sel(1'b1));  // open: D

  // Other names for the same wires on the sheet: clock = clk

  // Notes on the sheet:
  //   Instruction_Memory loads imem.mem
endmodule

/* Test case cpu:
clk ReadData1 ReadData2
*/
